// Logisim project Ammar --Final.circ as structural Verilog: 8 circuits, main circuit main
module main (
  input  Enable,
  input  Reset,
  output c1,
  output c0,
  output not_found,
  output found
);

  wire and_1_out, and_2_out, Clock_out, expected_output_1_out_5, not_2_out, not_4_out, not_5_out, or_1_out,
       test_ic_1_all_equal, test_ic_1_output, validate_1_out_4;
  wire [1:0] Main_Counter_q;
  wire [3:2] not_1_out;

  Clock Clock (.out(Clock_out));
  and and_1 (and_1_out, or_1_out, not_2_out);
  and and_2 (and_2_out, validate_1_out_4, Enable, or_1_out, not_found);
  Counter #(.width(4), .max('hf), .ongoal("continue")) Main_Counter (
    .load(and_1_out), .D({not_1_out, 2'b00}), .count(and_2_out), .Q({c1, c0, Main_Counter_q}),
    .clk(Clock_out), .clr(Reset));  // open: carry
  not not_1 (not_1_out[2], c0);
  expected_output expected_output_1 (
    .Test_Case_0(Main_Counter_q[1]), .Test_Case_1(Main_Counter_q[0]), .IC_Type_1(c1), .IC_Type_0(c0),
    .out_5(expected_output_1_out_5));
  xor xor_1 (not_1_out[3], c0, c1);
  not not_2 (not_2_out, validate_1_out_4);
  and and_3 (found, validate_1_out_4, Main_Counter_q[1], Main_Counter_q[0]);
  Test_Ic test_ic_1 (
    .A(Main_Counter_q[1]), .B(Main_Counter_q[0]), .Output(test_ic_1_output), .all_equal(test_ic_1_all_equal));
  or or_1 (or_1_out, validate_1_out_4, not_4_out, not_5_out);
  not not_3 (not_found, found);
  not not_4 (not_4_out, c1);
  not not_5 (not_5_out, c0);
  Validate validate_1 (
    .all_equal(test_ic_1_all_equal), .in_2(test_ic_1_output), .in_3(expected_output_1_out_5),
    .out_4(validate_1_out_4));
endmodule

// Expected Output
module expected_output (
  input  Test_Case_0,
  input  Test_Case_1,
  input  IC_Type_1,
  input  IC_Type_0,
  output out_5
);

  wire and_1_out, nand_1_out, or_1_out, xor_1_out;

  or or_1 (or_1_out, Test_Case_0, Test_Case_1);
  xor xor_1 (xor_1_out, Test_Case_0, Test_Case_1);
  nand nand_1 (nand_1_out, Test_Case_0, Test_Case_1);
  and and_1 (and_1_out, Test_Case_0, Test_Case_1);
  Multiplexer #(.select(2)) multiplexer_1 (
    .in0(and_1_out), .in1(or_1_out), .in2(xor_1_out), .in3(nand_1_out), .out(out_5),
    .sel({IC_Type_1, IC_Type_0}));  // open: en
endmodule

module Validate (
  input  all_equal,
  input  in_2,
  input  in_3,
  output out_4
);

  wire xnor_1_out;

  xnor xnor_1 (xnor_1_out, in_2, in_3);
  and and_1 (out_4, all_equal, xnor_1_out);
endmodule

module Success (
  input  Enable,
  input  validate,
  input  reset,
  output Q
);

  wire and_1_out;

  and and_1 (and_1_out, Q, validate);
  D_Flip_Flop d_ff_1 (.clk(Enable), .D(and_1_out), .Q(Q), .preset(reset), .en(Enable));  // open: Qn, reset

  // Notes on the sheet:
  //   this AND is only for simulation
endmodule

// Test IC
module Test_Ic (
  input  A,
  input  B,
  output Output,
  output all_equal
);

  wire or_2_out, or_3_out, or_4_out, xnor_1_out, xnor_2_out;

  or or_1 (Output, A, B);
  or or_2 (or_2_out, A, B);
  or or_3 (or_3_out, A, B);
  or or_4 (or_4_out, A, B);
  xnor xnor_1 (xnor_1_out, Output, or_2_out);
  xnor xnor_2 (xnor_2_out, or_3_out, or_4_out);
  and and_1 (all_equal, xnor_1_out, xnor_2_out);
  // NAND_Gate nand_1 is placed but not wired
  // NAND_Gate nand_2 is placed but not wired
  // NAND_Gate nand_3 is placed but not wired
  // NAND_Gate nand_4 is placed but not wired
  // XOR_Gate xor_1 is placed but not wired
  // XOR_Gate xor_2 is placed but not wired
  // XOR_Gate xor_3 is placed but not wired
  // XOR_Gate xor_4 is placed but not wired
  // OR_Gate or_5 is placed but not wired
  // OR_Gate or_6 is placed but not wired
  // OR_Gate or_7 is placed but not wired
  // OR_Gate or_8 is placed but not wired
  // AND_Gate and_2 is placed but not wired
  // AND_Gate and_3 is placed but not wired
  // AND_Gate and_4 is placed but not wired
  // AND_Gate and_5 is placed but not wired

  // Notes on the sheet:
  //   11
  //   10
  //   01
  //   00
endmodule

module optimiseCounter (
  input  nf,
  input  v,
  input  c3,
  input  nc2,
  output l,
  output e
);

  wire not_1_out, not_2_out, or_1_out;

  not not_1 (not_1_out, c3);
  or or_1 (or_1_out, not_1_out, nc2);
  not not_2 (not_2_out, v);
  and and_1 (e, nf, v);
  and and_2 (l, or_1_out, not_2_out);
endmodule

module _2_4_MUX (
  input  C0,
  input  C1,
  input  I0,
  input  I1,
  input  I2,
  input  I3,
  output O
);

  wire and_1_out, and_2_out, and_3_out, and_4_out, not_1_out, not_2_out, not_3_out, not_4_out;

  not not_1 (not_1_out, C0);
  not not_2 (not_2_out, C1);
  not not_3 (not_3_out, C0);
  not not_4 (not_4_out, C1);
  and and_1 (and_1_out, not_1_out, not_2_out, I0);
  and and_2 (and_2_out, not_3_out, C1, I1);
  and and_3 (and_3_out, C0, not_4_out, I2);
  and and_4 (and_4_out, C0, C1, I3);
  or or_1 (O, and_1_out, and_2_out, and_3_out, and_4_out);
endmodule

module _74LS161_4_bit_counter (
  input  I0,
  input  I1,
  input  I2,
  input  I3,
  input  ENP,
  input  ENT,
  input  CLK,
  input  nCLR,
  input  nLOAD,
  output Q0,
  output Q1,
  output Q2,
  output Q3,
  output RCO
);

  wire and_1_out, and_2_out, and_3_out, not_1_out, not_2_out, or_1_out;

  and and_1 (and_1_out, ENP, ENT, CLK, nLOAD);
  and and_2 (and_2_out, ENP, nLOAD);
  not not_1 (not_1_out, nCLR);
  not not_2 (not_2_out, nLOAD);
  or or_1 (or_1_out, not_2_out, and_3_out);
  and and_3 (and_3_out, and_1_out, nLOAD);
  Counter #(.width(4), .max('hf)) counter_1 (
    .load(not_2_out), .D({I3, I2, I1, I0}), .count(and_2_out), .Q({Q3, Q2, Q1, Q0}), .carry(RCO),
    .clk(or_1_out), .clr(not_1_out));
endmodule
