// Logisim project main.circ as structural Verilog: 4 circuits, main circuit main
module main (
  input  Enable,
  input  Reset,
  output c0,
  output c1,
  output not_found,
  output out_6
);

  wire and_1_out, Clock_out, expected_output_1_out_3, nand_1_out, or_1_out, validate_1_out_3;
  wire [1:0] Test_Case_Counter_q;

  Clock Clock (.out(Clock_out));
  and and_1 (and_1_out, Clock_out, not_found, Enable);
  nand nand_1 (nand_1_out, Test_Case_Counter_q[0], Test_Case_Counter_q[1]);
  Counter #(.width(2), .max('h3)) Main_Counter (
    .count(1'b1), .Q({c1, c0}), .clk(nand_1_out), .clr(Reset));  // open: load, D, carry
  Counter #(.width(2), .max('h3), .ongoal("continue")) Test_Case_Counter (
    .count(1'b1), .Q(Test_Case_Counter_q), .clk(and_1_out), .clr(Reset));  // open: load, D, carry
  expected_output expected_output_1 (.in_1({c1, c0}), .in_2(Test_Case_Counter_q), .out_3(expected_output_1_out_3));
  or or_1 (or_1_out, Test_Case_Counter_q[0], Test_Case_Counter_q[1]);
  Validate validate_1 (.in_1(or_1_out), .in_2(expected_output_1_out_3), .out_3(validate_1_out_3));
  Success success_1 (.clk(and_1_out), .validate(validate_1_out_3), .found(out_6), .not_found(not_found), .reset(Reset));
  // AND_Gate and_2 is placed but not wired
  // OR_Gate or_2 is placed but not wired
  // XOR_Gate xor_1 is placed but not wired
  // NAND_Gate nand_2 is placed but not wired

  // Notes on the sheet:
  //   Expected Output
  //   Test IC
  //   found
  //   validate
  //   success
endmodule

module expected_output (
  input  [1:0] in_1,
  input  [1:0] in_2,
  output out_3
);


  assign out_3 = 1'b1;

  // Notes on the sheet:
  //   this is not complete yet
endmodule

module Validate (
  input  in_1,
  input  in_2,
  output out_3
);

  xnor xnor_1 (out_3, in_1, in_2);
endmodule

module Success (
  input  clk,
  input  validate,
  input  reset,
  output found,
  output not_found
);

  wire and_1_out;

  and and_1 (and_1_out, validate, found);
  D_Flip_Flop d_ff_1 (.clk(clk), .D(and_1_out), .Q(found), .Qn(not_found), .reset(reset));  // open: preset, en
endmodule
